# Fritzing sketch Fritzing Sketch (saved by Fritzing 0.9.4)
breadboards: 1

parts:
  Part1 = Black Joystick KY-023
  Part2 = Arduino Uno (Rev3) - ICSP
  LED2 = RGB LED (com. cathode, rgb) [package="5 mm [THT]"]
  R1 = Resistor [tolerance=±5% resistance=330 package=THT]
  R2 = Resistor [tolerance=±5% resistance=330 package=THT]
  R3 = Resistor [tolerance=±5% resistance=330 package=THT]
  R4 = Resistor [tolerance=±5% resistance=1k package=THT]
  R5 = Resistor [tolerance=±5% resistance=1k package=THT]

nets:
  N1: Part1.VRy, R5.Pin_1
  N2: Part1.VRx, R4.Pin_1
  +5V: Part1.+5V, Part2.5V
  GND: Part1.GND, Part2.GND, LED2.common_cathode
  N3: Part2.A0, R4.Pin_0
  N4: Part2.A1, R5.Pin_0
  N5: Part2.D9_PWM, R3.Pin_0
  N6: Part2.D10_PWM/SS, R2.Pin_0
  N7: Part2.D11_PWM/MOSI, R1.Pin_0
  N8: LED2.red_anode, R1.Pin_1
  N9: LED2.green_anode, R2.Pin_1
  N10: LED2.blue_anode, R3.Pin_1

custom parts:
  Black Joystick KY-023: Description: The joystick is a combination of 2 analoog potentiometer and a digital switch. Arduino GND --> Module pin - Arduino +5V --> Module pin +5V Arduino Analoog 0 --> Module VRx Arduino Analoog 1 --> Module VRy Arduino Digital --> Module SW Dimensions: 1" x 1.25"
